// Logisim project Questão 1 - Modo A.circ as structural Verilog: 1 circuit, main circuit main
module main (
  input  in_1,
  input  Caixa_Vazia,
  output out_3
);

  wire not_1_out, or_1_out;

  not not_1 (not_1_out, in_1);
  or or_1 (or_1_out, not_1_out, Caixa_Vazia);
  buf and_1 (out_3, or_1_out);  // AND_Gate
  LED led_1 (.in(out_3));

  // Notes on the sheet:
  //   Bomba
  //   Modo A
  //   Caixa Cheia
endmodule
