// Logisim project Questão 1 - Modo B.circ as structural Verilog: 1 circuit, main circuit main
module main (
  input  in_1,
  input  Caixa_Vazia,
  input  Metade_da_caixa,
  output Caixa_Cheia
);

  wire not_1_out, not_2_out, not_3_out, or_1_out;

  not not_1 (not_1_out, in_1);
  not not_2 (not_2_out, Metade_da_caixa);
  LED led_1 (.in(Caixa_Vazia));
  or or_1 (or_1_out, not_1_out, Caixa_Vazia);
  and and_1 (Caixa_Cheia, or_1_out, not_2_out);
  LED led_2 (.in(not_3_out));
  not not_3 (not_3_out, Caixa_Cheia);

  // Notes on the sheet:
  //   Bomba
  //   Modo B
endmodule
