// Logisim project Questão 2 - A.circ as structural Verilog: 1 circuit, main circuit main
module main (
  input  A,
  input  B,
  input  C,
  input  D,
  output out_5
);

  wire A_nBD_out, nA_nB_nD_out, nA_nC_out, nC_nD_out, not_1_out, not_2_out, not_3_out, not_4_out;

  not not_1 (not_1_out, A);
  not not_2 (not_2_out, B);
  not not_3 (not_3_out, C);
  not not_4 (not_4_out, D);
  and nA_nC (nA_nC_out, not_3_out, not_1_out);
  and nA_nB_nD (nA_nB_nD_out, not_1_out, not_4_out, not_2_out);
  and A_nBD (A_nBD_out, A, not_2_out, D);
  and nC_nD (nC_nD_out, not_3_out, not_4_out);
  or or_1 (out_5, nA_nC_out, nA_nB_nD_out, A_nBD_out, nC_nD_out);

  // Notes on the sheet:
  //   ~A~C+~C~D+~A~B~D+A~BD
endmodule
