// Logisim project Questão 2 - B.circ as structural Verilog: 1 circuit, main circuit main
module main (
  input  A,
  input  B,
  input  C,
  input  D,
  output out_5
);

  wire A_nBD_out, B_nD_out, nA_nC_out, nA_nD_out, not_1_out, not_2_out, not_3_out, not_4_out;

  not not_1 (not_1_out, A);
  not not_2 (not_2_out, B);
  not not_3 (not_3_out, C);
  not not_4 (not_4_out, D);
  and A_nBD (A_nBD_out, A, not_2_out, D);
  and B_nD (B_nD_out, B, not_4_out);
  and nA_nC (nA_nC_out, not_1_out, not_3_out);
  and nA_nD (nA_nD_out, not_1_out, not_4_out);
  or or_1 (out_5, A_nBD_out, B_nD_out, nA_nC_out, nA_nD_out);

  // Notes on the sheet:
  //   A~BD+B~D+~A~C+~AD
endmodule
