// Logisim project Questão 3 - Codificador.circ as structural Verilog: 1 circuit, main circuit main
module main (
  input  A,
  input  B,
  input  C,
  input  D,
  output out_5,
  output out_6,
  output Johnson,
  output out_8,
  output out_9
);

  wire and_1_out, and_2_out, and_3_out, and_4_out, and_5_out, and_6_out, and_7_out, and_8_out, and_9_out,
       and_10_out, not_1_out, not_2_out, not_3_out, not_4_out, not_5_out, not_6_out, not_7_out, not_8_out;

  not not_1 (not_1_out, D);
  not not_2 (not_2_out, C);
  not not_3 (not_3_out, B);
  not not_4 (not_4_out, D);
  not not_5 (not_5_out, A);
  not not_6 (not_6_out, C);
  not not_7 (not_7_out, C);
  not not_8 (not_8_out, B);
  and and_1 (and_1_out, B, D);
  and and_2 (and_2_out, B, C);
  and and_3 (and_3_out, A, not_1_out);
  and and_4 (and_4_out, C, C);
  and and_5 (and_5_out, B, not_2_out);
  and and_6 (and_6_out, not_3_out, C);
  and and_7 (and_7_out, C, not_4_out);
  and and_8 (and_8_out, not_5_out, D, not_6_out);
  and and_9 (and_9_out, B, not_7_out);
  and and_10 (and_10_out, not_8_out, C);
  or or_1 (out_5, A, and_1_out, and_2_out);
  or or_2 (out_6, B, and_3_out);
  or or_3 (Johnson, B, and_4_out);
  or or_4 (out_8, and_5_out, and_6_out, and_7_out);
  or or_5 (out_9, and_8_out, and_9_out, and_10_out);

  // Notes on the sheet:
  //   BCD
endmodule
