// Logisim project Questão 4.circ as structural Verilog: 1 circuit, main circuit main
module main (
  input  A,
  input  B,
  input  C,
  output A_2,
  output B_2,
  output C_2
);

  wire and_1_out, and_2_out, not_1_out, not_2_out, not_3_out, not_4_out;

  not not_1 (not_1_out, B);
  not not_2 (not_2_out, C);
  not not_3 (not_3_out, A);
  not not_4 (not_4_out, B);
  and and_1 (and_1_out, A, B);
  and and_2 (and_2_out, not_1_out, not_2_out);
  and and_3 (B_2, not_3_out, B);
  and and_4 (C_2, C, not_4_out);
  or or_1 (A_2, and_1_out, and_2_out);

  // Notes on the sheet:
  //   Carros nas Ruas
  //   Semáforo
endmodule
