// Logisim project Passo 3.circ as structural Verilog: 1 circuit, main circuit main
module main (
  input  A,
  input  A_2,
  input  B,
  input  B_2,
  input  A_3,
  input  B_3,
  output S,
  output S_2,
  output S_3
);

  wire and_1_out, and_2_out, not_2_out, or_1_out, or_2_out;

  and and_1 (and_1_out, A, B);
  not not_1 (S, and_1_out);
  or or_1 (or_1_out, A_3, B_3);
  and and_2 (and_2_out, B_3, A_3);
  not not_2 (not_2_out, or_1_out);
  or or_2 (or_2_out, A_2, B_2);
  or or_3 (S_3, not_2_out, and_2_out);
  not not_3 (S_2, or_2_out);

  // Notes on the sheet:
  //   NAND
  //   XNOR
  //   NOR
endmodule
