// Logisim project Passo 4 - A.circ as structural Verilog: 1 circuit, main circuit main
module main (
  input  A,
  input  B,
  input  C,
  input  D,
  output n_AB_C_D
);

  wire and_1_out, and_2_out, or_1_out;

  and and_1 (and_1_out, A, B);
  or or_1 (or_1_out, C, D);
  and and_2 (and_2_out, and_1_out, or_1_out);
  not not_1 (n_AB_C_D, and_2_out);

  // Notes on the sheet:
  //   AB
  //   C+D
  //   AB(C+D)
endmodule
