// Logisim project Passo 4 - B.circ as structural Verilog: 1 circuit, main circuit main
module main (
  input  A,
  input  B,
  input  C,
  input  D,
  input  E,
  output out_6
);

  wire and_1_out, and_2_out, not_1_out, not_2_out, not_3_out, not_4_out, not_5_out, or_1_out, or_2_out;

  or or_1 (or_1_out, A, B);
  not not_1 (not_1_out, B);
  not not_2 (not_2_out, C);
  not not_3 (not_3_out, D);
  not not_4 (not_4_out, E);
  and and_1 (and_1_out, not_1_out, C, not_3_out);
  and and_2 (and_2_out, not_2_out, D, not_4_out);
  or or_2 (or_2_out, or_1_out, and_2_out);
  not not_5 (not_5_out, or_2_out);
  or or_3 (out_6, and_1_out, not_5_out);

  // Notes on the sheet:
  //   A+B
  //   ~B
  //   ~C
  //   ~D
  //   ~E
  //   ~BC~D
  //   ~CD~E
  //   A+B+~CD~E
  //   ~(A+B+~CD~E)
  //   ~(A+B+~CD~E)+~BC~D
endmodule
