// Logisim project Passo 4 - C.circ as structural Verilog: 1 circuit, main circuit main
module main (
  input  M,
  input  N,
  input  P,
  input  Q,
  output n_M_N__nPQ
);

  wire and_1_out, not_1_out, not_2_out, or_1_out;

  or or_1 (or_1_out, M, N);
  not not_1 (not_1_out, P);
  and and_1 (and_1_out, not_1_out, Q);
  not not_2 (not_2_out, or_1_out);
  or or_2 (n_M_N__nPQ, not_2_out, and_1_out);

  // Notes on the sheet:
  //   ~P
  //   M+N
  //   ~PQ
  //   ~(M+N)
endmodule
