// Logisim project Passo 5 - A.circ as structural Verilog: 1 circuit, main circuit main
module main (
  input  A,
  input  B,
  input  C,
  output n_nAB_nC,
  output A_nB_C
);

  wire and_1_out, not_1_out, not_2_out, not_3_out;

  not not_1 (not_1_out, A);
  not not_2 (not_2_out, C);
  not not_3 (not_3_out, B);
  and and_1 (and_1_out, not_1_out, B, not_2_out);
  or or_1 (A_nB_C, A, not_3_out, C);
  not not_4 (n_nAB_nC, and_1_out);

  // Notes on the sheet:
  //   ~A
  //   ~C
  //   ~B
  //   ~AB~C
endmodule
