// Logisim project Passo 5 - B.circ as structural Verilog: 1 circuit, main circuit main
module main (
  input  A,
  input  B,
  input  C,
  output n_nA_nBC,
  output A_B_nC
);

  wire and_1_out, not_1_out, not_2_out, not_3_out, or_1_out, or_2_out;

  not not_1 (not_1_out, C);
  not not_2 (not_2_out, A);
  not not_3 (not_3_out, B);
  and and_1 (and_1_out, not_3_out, C);
  or or_1 (or_1_out, B, not_1_out);
  and and_2 (A_B_nC, A, or_1_out);
  or or_2 (or_2_out, not_2_out, and_1_out);
  not not_4 (n_nA_nBC, or_2_out);

  // Notes on the sheet:
  //   ~A
  //   ~B
  //   ~C
  //   ~BC
  //   B+~C
  //   ~A+~BC
endmodule
