// Logisim project Passo 5 - C.circ as structural Verilog: 1 circuit, main circuit main
module main (
  input  A,
  input  B,
  input  C,
  input  D,
  output n_AB_n_CD,
  output nA_nB_CD
);

  wire and_1_out, and_2_out, and_3_out, and_4_out, not_1_out, not_2_out, not_3_out;

  and and_1 (and_1_out, A, B);
  and and_2 (and_2_out, C, D);
  not not_1 (not_1_out, A);
  not not_2 (not_2_out, B);
  and and_3 (and_3_out, D, C);
  not not_3 (not_3_out, and_2_out);
  and and_4 (and_4_out, and_1_out, not_3_out);
  or or_1 (nA_nB_CD, not_1_out, not_2_out, and_3_out);
  not not_4 (n_AB_n_CD, and_4_out);

  // Notes on the sheet:
  //   CD
  //   ~A
  //   ~B
  //   CD
  //   AB
  //   ~(CD)
  //   AB~(CD)
endmodule
