// Logisim project Passo 5 - D.circ as structural Verilog: 1 circuit, main circuit main
module main (
  input  A,
  input  B,
  output n_A_nB,
  output out_4
);

  wire not_1_out, not_2_out, or_1_out;

  not not_1 (not_1_out, B);
  not not_2 (not_2_out, A);
  or or_1 (or_1_out, A, not_1_out);
  and and_1 (out_4, not_2_out, B);
  not not_3 (n_A_nB, or_1_out);

  // Notes on the sheet:
  //   ~B
  //   ~A
  //   A+~B
  //   ~AB
endmodule
