// Logisim project Passo 5 - E.circ as structural Verilog: 1 circuit, main circuit main
module main (
  input  A,
  input  B,
  output n_n_AB,
  output out_4
);

  wire and_1_out, not_1_out;

  and and_1 (and_1_out, A, B);
  and and_2 (out_4, B, A);
  not not_1 (not_1_out, and_1_out);
  not not_2 (n_n_AB, not_1_out);

  // Notes on the sheet:
  //   AB
  //   ~(AB)
  //   AB
endmodule
