// Logisim project Passo 5 - F.circ as structural Verilog: 1 circuit, main circuit main
module main (
  input  A,
  input  C,
  input  D,
  output n_nA_nC_nD,
  output ACD
);

  wire not_1_out, not_2_out, not_3_out, or_1_out;

  not not_1 (not_1_out, A);
  not not_2 (not_2_out, C);
  not not_3 (not_3_out, D);
  or or_1 (or_1_out, not_1_out, not_2_out, not_3_out);
  and and_1 (ACD, A, C, D);
  not not_4 (n_nA_nC_nD, or_1_out);

  // Notes on the sheet:
  //   ~A
  //   ~C
  //   ~D
  //   ~A+~C+~D
endmodule
