// Logisim project Passo 5 - G.circ as structural Verilog: 1 circuit, main circuit main
module main (
  input  A,
  input  B,
  input  C,
  input  D,
  output n_A_n_B_nC__D,
  output nA__B_nC__nD
);

  wire and_1_out, not_1_out, not_2_out, not_3_out, not_4_out, not_5_out, or_1_out;

  not not_1 (not_1_out, C);
  not not_2 (not_2_out, A);
  not not_3 (not_3_out, C);
  not not_4 (not_4_out, D);
  or or_1 (or_1_out, B, not_1_out);
  not not_5 (not_5_out, or_1_out);
  or or_2 (nA__B_nC__nD, not_2_out, B, not_3_out, not_4_out);
  and and_1 (and_1_out, A, not_5_out, D);
  not not_6 (n_A_n_B_nC__D, and_1_out);

  // Notes on the sheet:
  //   ~C
  //   B+~C
  //   ~A
  //   ~C
  //   ~D
  //   ~(B+~C)
  //   A(~(B+~C))D
endmodule
