// Logisim project Passo 5 - H.circ as structural Verilog: 1 circuit, main circuit main
module main (
  input  M,
  input  N,
  output n__M_nN__nM_N,
  output M_XOR_N
);

  wire and_1_out, not_1_out, not_2_out, or_1_out, or_2_out;

  not not_1 (not_1_out, M);
  not not_2 (not_2_out, N);
  xor xor_1 (M_XOR_N, M, N);
  or or_1 (or_1_out, M, not_2_out);
  or or_2 (or_2_out, N, not_1_out);
  and and_1 (and_1_out, or_1_out, or_2_out);
  not not_3 (n__M_nN__nM_N, and_1_out);

  // Notes on the sheet:
  //   ~M
  //   ~N
  //   M+~N
  //   ~M+N
  //   (M+~N)(~M+N)
endmodule
