// Logisim project Passo 5 - I.circ as structural Verilog: 1 circuit, main circuit main
module main (
  input  A,
  input  B,
  input  C,
  input  D,
  output n_n_n_AB_C_D,
  output out_6
);

  wire and_1_out, and_2_out, and_3_out, and_4_out, not_1_out, not_2_out, not_3_out, not_4_out, not_5_out,
       or_1_out;

  and and_1 (and_1_out, A, B);
  not not_1 (not_1_out, and_1_out);
  not not_2 (not_2_out, A);
  not not_3 (not_3_out, B);
  or or_1 (or_1_out, not_2_out, not_3_out);
  not not_4 (not_4_out, D);
  and and_2 (and_2_out, not_1_out, C);
  not not_5 (not_5_out, and_2_out);
  and and_3 (and_3_out, or_1_out, C);
  and and_4 (and_4_out, not_5_out, D);
  or or_2 (out_6, and_3_out, not_4_out);
  not not_6 (n_n_n_AB_C_D, and_4_out);

  // Notes on the sheet:
  //   AB
  //   ~A
  //   ~B
  //   ~(AB)
  //   ~D
  //   ~(AB)C
  //   ~A+~B
  //   ~[~(AB)C]
  //   (~A+~B)C
  //   ~[~(AB)C]D
  //   [(~A+~B)C]~D
endmodule
