// Logisim project Atividade 05 - B.circ as structural Verilog: 1 circuit, main circuit main
module main (
  input  T,
  input  P,
  input  R,
  output out_4
);

  wire nand_1_out, nand_2_out, nand_3_out;

  nand nand_1 (nand_1_out, P, P);
  nand nand_2 (nand_2_out, nand_1_out, R);
  nand nand_3 (nand_3_out, T, nand_2_out);
  nand nand_4 (out_4, nand_3_out, nand_3_out);

  // Notes on the sheet:
  //   ~(PP)
  //   ~(~(PP)R)
  //   ~(~(~(PP)R)T)
  //   ~(~(~(~(PP)R)T) ~(~(~(PP)R)T))
endmodule
