// Logisim project Atividade 06 - A.circ as structural Verilog: 1 circuit, main circuit main
module main (
  input  A,
  input  B,
  input  C,
  input  D,
  output n_AB_C_D
);

  wire and_1_out, or_1_out;

  and and_1 (and_1_out, A, B);
  or or_1 (or_1_out, C, D);
  nand nand_1 (n_AB_C_D, and_1_out, or_1_out);

  // Notes on the sheet:
  //   AB
  //   C+D
endmodule
