// Logisim project Atividade 06 - B.circ as structural Verilog: 1 circuit, main circuit main
module main (
  input  in_1,
  input  in_2,
  input  in_3,
  input  in_4,
  input  in_5,
  output out_6
);

  wire and_1_out, and_2_out, nor_1_out, not_1_out, not_2_out, not_3_out, not_4_out, or_1_out;

  or or_1 (or_1_out, in_1, in_2);
  not not_1 (not_1_out, in_2);
  not not_2 (not_2_out, in_3);
  not not_3 (not_3_out, in_4);
  not not_4 (not_4_out, in_5);
  and and_1 (and_1_out, not_1_out, in_3, not_3_out);
  and and_2 (and_2_out, not_2_out, in_4, not_4_out);
  nor nor_1 (nor_1_out, or_1_out, and_2_out);
  or or_2 (out_6, and_1_out, nor_1_out);

  // Notes on the sheet:
  //   A+B
  //   ~B
  //   ~C
  //   ~D
  //   ~E
  //   ~BC~D
  //   ~CD~E
  //   ~(A+B+~CD~E)
  //   ~(A+B+~CD~E)+~BC~D
endmodule
