// Logisim project Atividade 06 - C.circ as structural Verilog: 1 circuit, main circuit main
module main (
  input  M,
  input  N,
  input  P,
  input  Q,
  output n_M_N__nPQ
);

  wire and_1_out, nor_1_out, not_1_out;

  not not_1 (not_1_out, P);
  nor nor_1 (nor_1_out, M, N);
  and and_1 (and_1_out, not_1_out, Q);
  or or_1 (n_M_N__nPQ, nor_1_out, and_1_out);

  // Notes on the sheet:
  //   ~P
  //   ~(M+N)
  //   ~PQ
endmodule
