// Logisim project Atividade 06 - D.circ as structural Verilog: 1 circuit, main circuit main
module main (
  input  W,
  input  P,
  input  Q,
  output n_W_P_nQ
);

  wire and_1_out, not_1_out;

  not not_1 (not_1_out, Q);
  and and_1 (and_1_out, P, not_1_out);
  nor nor_1 (n_W_P_nQ, W, and_1_out);

  // Notes on the sheet:
  //   ~Q
  //   P~Q
endmodule
