// Logisim project Atividade 06 - E.circ as structural Verilog: 1 circuit, main circuit main
module main (
  input  M,
  input  N,
  input  P,
  output MN_P_nN
);

  wire and_1_out, not_1_out, or_1_out;

  not not_1 (not_1_out, N);
  and and_1 (and_1_out, M, N);
  or or_1 (or_1_out, not_1_out, P);
  and and_2 (MN_P_nN, and_1_out, or_1_out);

  // Notes on the sheet:
  //   ~N
  //   MN
  //   P+~N
endmodule
