// Logisim project Atividade 06 - F.circ as structural Verilog: 1 circuit, main circuit main
module main (
  input  A,
  input  B,
  output A_B__nA_nB
);

  wire not_1_out, not_2_out, or_1_out, or_2_out;

  not not_1 (not_1_out, A);
  not not_2 (not_2_out, B);
  or or_1 (or_1_out, A, B);
  or or_2 (or_2_out, not_2_out, not_1_out);
  and and_1 (A_B__nA_nB, or_1_out, or_2_out);

  // Notes on the sheet:
  //   ~A
  //   ~B
  //   A+B
  //   ~A+~B
endmodule
