// Logisim project Atividade 03 - A.circ as structural Verilog: 1 circuit, main circuit main
module main (
  input  A,
  input  B,
  input  C,
  output nAC_BC
);

  wire and_1_out, and_2_out, not_1_out;

  not not_1 (not_1_out, A);
  and and_1 (and_1_out, not_1_out, C);
  and and_2 (and_2_out, B, C);
  or or_1 (nAC_BC, and_1_out, and_2_out);

  // Notes on the sheet:
  //   ~A
  //   ~AC
  //   BC
endmodule
