// Logisim project Atividade 03 - B.circ as structural Verilog: 1 circuit, main circuit main
module main (
  input  Q,
  input  R,
  output nQR_Q_nR
);

  wire and_1_out, and_2_out, not_1_out, not_2_out;

  not not_1 (not_1_out, Q);
  not not_2 (not_2_out, R);
  and and_1 (and_1_out, not_1_out, R);
  and and_2 (and_2_out, not_2_out, Q);
  or or_1 (nQR_Q_nR, and_1_out, and_2_out);

  // Notes on the sheet:
  //   ~Q
  //   ~R
  //   ~QR
  //   Q~R
endmodule
