// Logisim project Atividade 03 - C.circ as structural Verilog: 1 circuit, main circuit main
module main (
  input  A,
  input  C,
  output nA_C
);

  wire not_1_out;

  not not_1 (not_1_out, A);
  or or_1 (nA_C, not_1_out, C);

  // Notes on the sheet:
  //   ~A
endmodule
