// Logisim project Atividade 03 - D.circ as structural Verilog: 1 circuit, main circuit main
module main (
  input  A,
  input  B,
  input  C,
  output A_nB_nB_nC_BC
);

  wire and_1_out, and_2_out, and_3_out, not_1_out, not_2_out;

  not not_1 (not_1_out, B);
  not not_2 (not_2_out, C);
  and and_1 (and_1_out, A, not_1_out);
  and and_2 (and_2_out, not_1_out, not_2_out);
  and and_3 (and_3_out, B, C);
  or or_1 (A_nB_nB_nC_BC, and_1_out, and_2_out, and_3_out);

  // Notes on the sheet:
  //   ~B
  //   ~C
  //   A~B
  //   ~B~C
  //   BC
endmodule
