// Logisim project Atividade 04 - A.circ as structural Verilog: 1 circuit, main circuit main
module main (
  input  A,
  input  B,
  input  C,
  input  D,
  output nA_nC_nBC_AC_nD
);

  wire and_1_out, and_2_out, and_3_out, not_1_out, not_2_out, not_3_out, not_4_out;

  not not_1 (not_1_out, A);
  not not_2 (not_2_out, C);
  not not_3 (not_3_out, B);
  not not_4 (not_4_out, D);
  and and_1 (and_1_out, not_1_out, not_2_out);
  and and_2 (and_2_out, not_3_out, C);
  and and_3 (and_3_out, A, C, not_4_out);
  or or_1 (nA_nC_nBC_AC_nD, and_1_out, and_2_out, and_3_out);

  // Notes on the sheet:
  //   ~A
  //   ~C
  //   ~B
  //   ~D
  //   ~A~C
  //   ~BC
  //   AC~D
endmodule
