// Logisim project Atividade 04 - B.circ as structural Verilog: 1 circuit, main circuit main
module main (
  input  A,
  input  B,
  input  C,
  input  D,
  output nA_nD_nB_nD_nBC
);

  wire and_1_out, and_2_out, and_3_out, not_1_out, not_2_out, not_3_out;

  not not_1 (not_1_out, A);
  not not_2 (not_2_out, B);
  not not_3 (not_3_out, D);
  and and_1 (and_1_out, not_1_out, not_3_out);
  and and_2 (and_2_out, not_2_out, not_3_out);
  and and_3 (and_3_out, not_2_out, C);
  or or_1 (nA_nD_nB_nD_nBC, and_1_out, and_2_out, and_3_out);

  // Notes on the sheet:
  //   ~A
  //   ~D
  //   ~B
  //   ~B
  //   ~A~D
  //   ~B~D
  //   ~BC
endmodule
