// Logisim project Atividade 04 - C.circ as structural Verilog: 1 circuit, main circuit main
module main (
  input  A,
  input  B,
  input  C,
  output nB_A_nC
);

  wire and_1_out, not_1_out, not_2_out;

  not not_1 (not_1_out, C);
  not not_2 (not_2_out, B);
  and and_1 (and_1_out, A, not_1_out);
  or or_1 (nB_A_nC, and_1_out, not_2_out);

  // Notes on the sheet:
  //   ~B
  //   A~C
endmodule
