// Logisim project Atividade 05 - A.circ as structural Verilog: 1 circuit, main circuit main
module main (
  input  D,
  input  C,
  input  B,
  input  A,
  output DA___nCB
);

  wire and_1_out, and_2_out, not_1_out;

  not not_1 (not_1_out, C);
  and and_1 (and_1_out, D, A);
  and and_2 (and_2_out, not_1_out, B);
  or or_1 (DA___nCB, and_1_out, and_2_out);

  // Notes on the sheet:
  //   DA
  //   ~CB
endmodule
