// Logisim project Atividade 03 - Subtrator.circ as structural Verilog: 1 circuit, main circuit main
module main (
  input  A,
  input  B,
  input  Borrow_In,
  output Diff,
  output Borrow_Out
);

  wire and_1_out, and_2_out, and_3_out, not_1_out, not_2_out, xor_1_out;

  not not_1 (not_1_out, A);
  not not_2 (not_2_out, A);
  xor xor_1 (xor_1_out, A, B);
  and and_1 (and_1_out, B, Borrow_In);
  and and_2 (and_2_out, not_1_out, Borrow_In);
  and and_3 (and_3_out, not_2_out, B);
  xor xor_2 (Diff, xor_1_out, Borrow_In);
  or or_1 (Borrow_Out, and_1_out, and_2_out, and_3_out);
endmodule
