// Logisim project Atividade 04 - Somador com Portas NAND.circ as structural Verilog: 1 circuit, main circuit main
module main (
  input  B,
  input  Carry_In,
  input  in_3,
  output Sum,
  output Carry_Out
);

  wire nand_1_out, nand_2_out, nand_3_out, nand_4_out, nand_5_out, nand_6_out, nand_7_out, nand_8_out,
       nand_9_out, nand_10_out, nand_11_out, nand_12_out, nand_13_out;

  nand nand_1 (nand_1_out, B, B);
  nand nand_2 (nand_2_out, Carry_In, Carry_In);
  nand nand_3 (nand_3_out, B, B);
  nand nand_4 (nand_4_out, in_3, in_3);
  nand nand_5 (nand_5_out, Carry_In, Carry_In);
  nand nand_6 (nand_6_out, in_3, in_3);
  nand nand_7 (nand_7_out, Carry_In, in_3);
  nand nand_8 (nand_8_out, B, in_3);
  nand nand_9 (nand_9_out, B, Carry_In);
  nand nand_10 (nand_10_out, nand_1_out, nand_2_out, in_3);
  nand nand_11 (nand_11_out, nand_3_out, Carry_In, nand_4_out);
  nand nand_12 (nand_12_out, B, nand_5_out, nand_6_out);
  nand nand_13 (nand_13_out, B, Carry_In, in_3);
  nand nand_14 (Carry_Out, nand_7_out, nand_8_out, nand_9_out);
  nand nand_15 (Sum, nand_10_out, nand_11_out, nand_12_out, nand_13_out);
endmodule
